// Logisim project control-logic.circ as structural Verilog: 1 circuit, main circuit control_logic
module control_logic (
  input  [31:0] Instruction,
  input  BrEq,
  input  BrLt,
  output PCSel,
  output RegWEn,
  output [2:0] ImmSel,
  output BrUn,
  output ASel,
  output BSel,
  output [3:0] ALUSel,
  output MemWEn,
  output [1:0] WBSel
);

  wire add, addi, alu_and, alu_mul, alu_mulh, alu_mulhu, alu_or, alu_sll, alu_slt, alu_sra, alu_srl, alu_sub,
       alu_xor, and1, and_1_out, and_2_out, and_3_out, and_4_out, and_5_out, and_6_out, and_7_out,
       and_13_out, and_14_out, and_18_out, and_19_out, and_20_out, and_21_out, and_22_out, and_23_out,
       and_24_out, and_25_out, and_26_out, and_27_out, and_28_out, and_29_out, and_30_out, and_31_out,
       and_32_out, and_33_out, and_46_out, and_47_out, and_48_out, and_49_out, and_50_out, and_51_out,
       and_59_out, and_60_out, and_61_out, and_62_out, andi, B_type, beq, bge, bgeu, blt, bltu, bne,
       comparator_6_eq, comparator_7_eq, comparator_8_eq, comparator_9_eq, comparator_10_eq,
       comparator_11_eq, comparator_12_eq, comparator_13_eq, comparator_14_eq, comparator_15_eq,
       comparator_16_eq, comparator_17_eq, comparator_18_eq, comparator_19_eq, comparator_20_eq,
       comparator_21_eq, comparator_22_eq, comparator_23_eq, comparator_24_eq, comparator_25_eq,
       comparator_26_eq, comparator_27_eq, comparator_28_eq, comparator_29_eq, comparator_30_eq,
       comparator_31_eq, comparator_32_eq, comparator_33_eq, comparator_34_eq, comparator_35_eq,
       comparator_36_eq, comparator_37_eq, comparator_38_eq, comparator_39_eq, comparator_40_eq,
       comparator_41_eq, I_type_imm, lui, not_1_out, not_2_out, or1, or_8_out, or_9_out, ori, R_type, sll1,
       slli, slt, slti, sra1, srai, srl1, srli, U_type_imm, xor1, xori;

  Comparator #(.width(7)) comparator_1 (.a(Instruction[6:0]), .b(7'b0010011), .eq(I_type_imm));  // open: gt, lt
  Comparator #(.width(7)) comparator_2 (.a(Instruction[6:0]), .b(7'b0110011), .eq(R_type));  // open: gt, lt
  Comparator #(.width(7)) comparator_3 (.a(Instruction[6:0]), .b(7'b1100011), .eq(B_type));  // open: gt, lt
  Comparator #(.width(7)) comparator_4 (.a(Instruction[6:0]), .b(7'b0110111), .eq(U_type_imm));  // open: gt, lt
  Comparator #(.width(7)) comparator_5 (.a(Instruction[6:0]), .b(7'b1100011), .eq(B_type));  // open: gt, lt
  and and_1 (and_1_out, I_type_imm, 1'b1);
  Comparator #(.width(3)) comparator_6 (.a(Instruction[14:12]), .b(3'b000), .eq(comparator_6_eq));  // open: gt, lt
  and and_2 (and_2_out, I_type_imm, 1'b1);
  Comparator #(.width(3)) comparator_7 (.a(Instruction[14:12]), .b(3'b111), .eq(comparator_7_eq));  // open: gt, lt
  and and_3 (and_3_out, I_type_imm, 1'b1);
  Comparator #(.width(3)) comparator_8 (.a(Instruction[14:12]), .b(3'b110), .eq(comparator_8_eq));  // open: gt, lt
  and and_4 (and_4_out, I_type_imm, 1'b1);
  Comparator #(.width(3)) comparator_9 (.a(Instruction[14:12]), .b(3'b100), .eq(comparator_9_eq));  // open: gt, lt
  and and_5 (and_5_out, I_type_imm, 1'b1);
  Comparator #(.width(3)) comparator_10 (.a(Instruction[14:12]), .b(3'b010), .eq(comparator_10_eq));  // open: gt, lt
  and and_6 (and_6_out, I_type_imm, 1'b1);
  Comparator #(.width(3)) comparator_11 (.a(Instruction[14:12]), .b(3'b001), .eq(comparator_11_eq));  // open: gt, lt
  and and_7 (and_7_out, I_type_imm, 1'b1);
  Comparator #(.width(3)) comparator_12 (.a(Instruction[14:12]), .b(3'b101), .eq(comparator_12_eq));  // open: gt, lt
  and and_8 (addi, and_1_out, comparator_6_eq);
  and and_9 (andi, and_2_out, comparator_7_eq);
  and and_10 (ori, and_3_out, comparator_8_eq);
  and and_11 (xori, and_4_out, comparator_9_eq);
  and and_12 (slti, and_5_out, comparator_10_eq);
  and and_13 (and_13_out, and_6_out, comparator_11_eq);
  and and_14 (and_14_out, and_7_out, comparator_12_eq);
  and and_15 (slli, and_13_out, comparator_13_eq);
  Comparator #(.width(7)) comparator_13 (.a(Instruction[31:25]), .b({7{1'b0}}), .eq(comparator_13_eq));  // open: gt, lt
  Comparator #(.width(7)) comparator_14 (.a(Instruction[31:25]), .b({7{1'b0}}), .eq(comparator_14_eq));  // open: gt, lt
  Comparator #(.width(7)) comparator_15 (
    .a(Instruction[31:25]), .b(7'b0100000), .eq(comparator_15_eq));  // open: gt, lt
  and and_16 (srli, and_14_out, comparator_14_eq);
  and and_17 (srai, and_14_out, comparator_15_eq);
  and and_18 (and_18_out, R_type, 1'b1);
  Comparator #(.width(3)) comparator_16 (.a(Instruction[14:12]), .b(3'b000), .eq(comparator_16_eq));  // open: gt, lt
  and and_19 (and_19_out, R_type, 1'b1);
  Comparator #(.width(3)) comparator_17 (.a(Instruction[14:12]), .b(3'b001), .eq(comparator_17_eq));  // open: gt, lt
  and and_20 (and_20_out, R_type, 1'b1);
  Comparator #(.width(3)) comparator_18 (.a(Instruction[14:12]), .b(3'b010), .eq(comparator_18_eq));  // open: gt, lt
  and and_21 (and_21_out, R_type, 1'b1);
  Comparator #(.width(3)) comparator_19 (.a(Instruction[14:12]), .b(3'b011), .eq(comparator_19_eq));  // open: gt, lt
  and and_22 (and_22_out, R_type, 1'b1);
  Comparator #(.width(3)) comparator_20 (.a(Instruction[14:12]), .b(3'b100), .eq(comparator_20_eq));  // open: gt, lt
  and and_23 (and_23_out, R_type, 1'b1);
  Comparator #(.width(3)) comparator_21 (.a(Instruction[14:12]), .b(3'b101), .eq(comparator_21_eq));  // open: gt, lt
  and and_24 (and_24_out, R_type, 1'b1);
  Comparator #(.width(3)) comparator_22 (.a(Instruction[14:12]), .b(3'b110), .eq(comparator_22_eq));  // open: gt, lt
  and and_25 (and_25_out, R_type, 1'b1);
  Comparator #(.width(3)) comparator_23 (.a(Instruction[14:12]), .b(3'b111), .eq(comparator_23_eq));  // open: gt, lt
  and and_26 (and_26_out, and_18_out, comparator_16_eq);
  and and_27 (and_27_out, and_19_out, comparator_17_eq);
  and and_28 (and_28_out, and_20_out, comparator_18_eq);
  and and_29 (and_29_out, and_21_out, comparator_19_eq);
  and and_30 (and_30_out, and_22_out, comparator_20_eq);
  and and_31 (and_31_out, and_23_out, comparator_21_eq);
  and and_32 (and_32_out, and_24_out, comparator_22_eq);
  and and_33 (and_33_out, and_25_out, comparator_23_eq);
  Comparator #(.width(7)) comparator_24 (.a(Instruction[31:25]), .b({7{1'b0}}), .eq(comparator_24_eq));  // open: gt, lt
  Comparator #(.width(7)) comparator_25 (
    .a(Instruction[31:25]), .b(7'b0100000), .eq(comparator_25_eq));  // open: gt, lt
  Comparator #(.width(7)) comparator_26 (
    .a(Instruction[31:25]), .b(7'b0000001), .eq(comparator_26_eq));  // open: gt, lt
  Comparator #(.width(7)) comparator_27 (.a(Instruction[31:25]), .b({7{1'b0}}), .eq(comparator_27_eq));  // open: gt, lt
  Comparator #(.width(7)) comparator_28 (
    .a(Instruction[31:25]), .b(7'b0000001), .eq(comparator_28_eq));  // open: gt, lt
  Comparator #(.width(7)) comparator_29 (.a(Instruction[31:25]), .b({7{1'b0}}), .eq(comparator_29_eq));  // open: gt, lt
  Comparator #(.width(7)) comparator_30 (
    .a(Instruction[31:25]), .b(7'b0000001), .eq(comparator_30_eq));  // open: gt, lt
  Comparator #(.width(7)) comparator_31 (.a(Instruction[31:25]), .b({7{1'b0}}), .eq(comparator_31_eq));  // open: gt, lt
  Comparator #(.width(7)) comparator_32 (.a(Instruction[31:25]), .b({7{1'b0}}), .eq(comparator_32_eq));  // open: gt, lt
  Comparator #(.width(7)) comparator_33 (
    .a(Instruction[31:25]), .b(7'b0100000), .eq(comparator_33_eq));  // open: gt, lt
  Comparator #(.width(7)) comparator_34 (.a(Instruction[31:25]), .b({7{1'b0}}), .eq(comparator_34_eq));  // open: gt, lt
  Comparator #(.width(7)) comparator_35 (.a(Instruction[31:25]), .b({7{1'b0}}), .eq(comparator_35_eq));  // open: gt, lt
  and and_34 (add, and_26_out, comparator_24_eq);
  and and_35 (alu_sub, and_26_out, comparator_25_eq);
  and and_36 (alu_mul, and_26_out, comparator_26_eq);
  and and_37 (sll1, and_27_out, comparator_27_eq);
  and and_38 (alu_mulh, and_27_out, comparator_28_eq);
  and and_39 (slt, and_28_out, comparator_29_eq);
  and and_40 (alu_mulhu, and_29_out, comparator_30_eq);
  and and_41 (xor1, and_30_out, comparator_31_eq);
  and and_42 (srl1, and_31_out, comparator_32_eq);
  and and_43 (sra1, and_31_out, comparator_33_eq);
  and and_44 (or1, and_32_out, comparator_34_eq);
  and and_45 (and1, and_33_out, comparator_35_eq);
  and and_46 (and_46_out, B_type, 1'b1);
  Comparator #(.width(3)) comparator_36 (.a(Instruction[14:12]), .b(3'b000), .eq(comparator_36_eq));  // open: gt, lt
  and and_47 (and_47_out, B_type, 1'b1);
  Comparator #(.width(3)) comparator_37 (.a(Instruction[14:12]), .b(3'b101), .eq(comparator_37_eq));  // open: gt, lt
  and and_48 (and_48_out, B_type, 1'b1);
  Comparator #(.width(3)) comparator_38 (.a(Instruction[14:12]), .b(3'b111), .eq(comparator_38_eq));  // open: gt, lt
  and and_49 (and_49_out, B_type, 1'b1);
  Comparator #(.width(3)) comparator_39 (.a(Instruction[14:12]), .b(3'b100), .eq(comparator_39_eq));  // open: gt, lt
  and and_50 (and_50_out, B_type, 1'b1);
  Comparator #(.width(3)) comparator_40 (.a(Instruction[14:12]), .b(3'b110), .eq(comparator_40_eq));  // open: gt, lt
  and and_51 (and_51_out, B_type, 1'b1);
  Comparator #(.width(3)) comparator_41 (.a(Instruction[14:12]), .b(3'b001), .eq(comparator_41_eq));  // open: gt, lt
  or or_1 (alu_sll, slli, sll1);
  or or_2 (alu_slt, slti, slt);
  or or_3 (alu_xor, xori, xor1);
  or or_4 (alu_srl, srli, srl1);
  or or_5 (alu_or, ori, or1);
  or or_6 (alu_and, andi, and1);
  or or_7 (alu_sra, srai, sra1);
  and and_52 (beq, and_46_out, comparator_36_eq);
  and and_53 (bge, and_47_out, comparator_37_eq);
  and and_54 (bgeu, and_48_out, comparator_38_eq);
  and and_55 (blt, and_49_out, comparator_39_eq);
  and and_56 (bltu, and_50_out, comparator_40_eq);
  and and_57 (bne, and_51_out, comparator_41_eq);
  or or_8 (or_8_out, blt, bltu);
  and and_58 (lui, U_type_imm, 1'b1);
  not not_1 (not_1_out, BrLt);
  or or_9 (or_9_out, bge, bgeu);
  and and_59 (and_59_out, BrEq, beq);
  and and_60 (and_60_out, not_1_out, or_9_out);
  and and_61 (and_61_out, BrLt, or_8_out);
  or or_10 (ALUSel[0], alu_sll, alu_srl, alu_and, alu_mulh, alu_mulhu, alu_sra, lui);
  or or_11 (ALUSel[1], alu_slt, alu_or, alu_and, alu_mulhu, lui);
  or or_12 (ALUSel[2], alu_xor, alu_or, alu_srl, alu_and, alu_sub, alu_sra, lui);
  or or_13 (ALUSel[3], alu_mul, alu_mulh, alu_mulhu, alu_sub, alu_sra, lui);
  not not_2 (not_2_out, BrEq);
  and and_62 (and_62_out, bne, not_2_out);
  buf or_14 (ASel, B_type);  // OR_Gate
  or or_15 (PCSel, and_60_out, and_59_out, and_61_out, and_62_out);
  or or_16 (BSel, I_type_imm, B_type);

  // Other names for the same wires on the sheet: Opcode[6:0] = Instruction[6:0]; rd[4:0] = Instruction[11:7];
  //   funct3[2:0] = Instruction[14:12]; funct7[6:0] = Instruction[31:25]; mul = alu_mul; mulh = alu_mulh;
  //   mulhu = alu_mulhu; sub = alu_sub

  // Notes on the sheet:
  //   INPUTS to your circuit
  //   DON'T CHANGE THE LOCATIONS OF THE INPUTS AND OUTPUTS!
  //   OUTPUT from your circuit
endmodule
